# Fritzing sketch teensypinsreference (saved by Fritzing 0.9.2b)
circuit board: 8.46667cm x 5.64444cm
perfboards: 1

parts:
  Teensy_3_1 = Teensy 3.1
  J1 = screw terminal, 3 pins
  J2 = screw terminal, 3 pins
  J3 = screw terminal, 3 pins
  J4 = screw terminal, 3 pins

nets:
  N1: Teensy_3_1.GND, J1.pin1, J2.pin1, J3.pin1, J4.pin3
  N2: Teensy_3_1.D1, J3.pin3
  N3: Teensy_3_1.D3, J3.pin2
  N4: Teensy_3_1.D5, J2.pin3
  N5: Teensy_3_1.D8, J2.pin2
  N6: Teensy_3_1.D10, J1.pin3
  N7: Teensy_3_1.D12, J1.pin2
  N8: Teensy_3_1.A2/D16, J4.pin2
  N9: Teensy_3_1.A5/D19, J4.pin1

notes:
  channel, data, clock
  1, 12, 10
  2, 16, 19
  3, 8, 5
  4, 3, 1
  channel 1
  channel 2
  channel 3
  channel 4
